// Logisim project circuitos.circ as structural Verilog: 1 circuit, main circuit main
module main (
  input  A,
  input  A_2,
  input  B,
  input  B_2,
  input  A_3,
  input  in_6,
  input  B_3,
  input  in_8,
  input  A_4,
  input  B_4,
  input  A_5,
  input  B_5,
  input  in_13,
  input  in_14,
  input  A_6,
  input  B_6,
  output out_17,
  output out_18,
  output out_19,
  output out_20,
  output out_21,
  output out_22,
  output out_23,
  output out_24
);

  wire nand_1_out, nand_2_out, nand_3_out, nand_4_out, nand_5_out, nand_6_out, nand_7_out, nand_8_out,
       nand_9_out, nand_10_out, nand_12_out, nand_14_out, nand_15_out, nand_17_out, nand_18_out, nand_19_out,
       nand_20_out, nor_1_out, nor_2_out, nor_3_out, nor_4_out, nor_6_out, nor_7_out, nor_9_out, nor_10_out,
       nor_11_out, nor_12_out, nor_14_out, nor_15_out, nor_16_out;

  nand nand_1 (nand_1_out, B_4, B_4);
  nand nand_2 (nand_2_out, in_13, in_13);
  nand nand_3 (nand_3_out, in_13, in_14);
  nand nand_4 (nand_4_out, in_14, in_14);
  nand nand_5 (nand_5_out, A_2, A_2);
  nand nand_6 (nand_6_out, B, B);
  nor nor_1 (nor_1_out, A_3, A_3);
  nand nand_7 (nand_7_out, A_4, A_4);
  nand nand_8 (nand_8_out, nand_1_out, nand_1_out);
  nand nand_9 (nand_9_out, nand_2_out, nand_3_out);
  nand nand_10 (nand_10_out, nand_3_out, nand_4_out);
  nor nor_2 (nor_2_out, A_6, A_6);
  nor nor_3 (nor_3_out, B_6, B_6);
  nand nand_11 (out_18, nand_12_out, nand_12_out);
  nand nand_12 (nand_12_out, nand_5_out, nand_6_out);
  nor nor_4 (nor_4_out, nor_1_out, B_3);
  nor nor_5 (out_19, nor_4_out, nor_4_out);
  nand nand_13 (out_21, nand_7_out, nand_8_out);
  nand nand_14 (nand_14_out, nand_9_out, nand_10_out);
  nor nor_6 (nor_6_out, nor_2_out, nor_2_out);
  nand nand_15 (nand_15_out, nand_14_out, nand_14_out);
  nor nor_7 (nor_7_out, nor_6_out, nor_3_out);
  nand nand_16 (out_23, nand_15_out, nand_15_out);
  nor nor_8 (out_24, nor_7_out, nor_7_out);
  nor nor_9 (nor_9_out, A, A);
  nand nand_17 (nand_17_out, in_6, in_8);
  nor nor_10 (nor_10_out, A_5, B_5);
  nor nor_11 (nor_11_out, nor_9_out, nor_9_out);
  nor nor_12 (nor_12_out, B_2, B_2);
  nand nand_18 (nand_18_out, in_6, nand_17_out);
  nand nand_19 (nand_19_out, nand_17_out, in_8);
  nor nor_13 (out_17, nor_11_out, nor_12_out);
  nand nand_20 (nand_20_out, nand_18_out, nand_19_out);
  nor nor_14 (nor_14_out, A_5, nor_10_out);
  nor nor_15 (nor_15_out, nor_14_out, nor_16_out);
  nor nor_16 (nor_16_out, nor_10_out, B_5);
  nand nand_21 (out_20, nand_20_out, nand_20_out);
  nor nor_17 (out_22, nor_15_out, nor_15_out);

  // Notes on the sheet:
  //   ~(~A^~B) NAND Q07
  //   (~A | B) NOR   Q02
  //   (A|~B) NAND  Q03
  //   Q01
  //   (~A & ~B)
  //   ~(~A&B) NOR Q08
  //   ~(A ^B) NANDQ 05
  //   (A^B) NOR Q06
  //   (~A & B)  NOR  Q 04 
endmodule
