// Logisim project confereRespostas.circ as structural Verilog: 1 circuit, main circuit main
module main (
  input  C,
  input  A,
  input  A_2,
  input  C_2,
  input  A_3,
  input  B,
  input  A_4,
  input  B_2,
  input  B_3,
  input  B_4,
  input  a_5,
  input  C_3,
  input  C_4,
  input  c_5,
  input  A_6,
  input  A_7,
  input  D,
  input  b_5,
  input  B_6,
  input  C_6,
  input  B_7,
  input  A_8,
  input  B_8,
  input  X,
  input  Y,
  input  Z,
  input  A_9,
  input  C_7,
  input  C_8,
  input  B_9,
  input  A_10,
  input  B_10,
  input  C_9,
  input  A_11,
  input  C_10,
  input  A_12,
  input  B_11,
  input  B_12,
  input  C_11,
  input  A_13,
  input  C_12,
  input  B_13,
  input  A_14,
  input  C_13,
  input  B_14,
  output out_46,
  output out_47,
  output out_48,
  output out_49,
  output out_50,
  output out_51,
  output out_52,
  output out_53,
  output out_54,
  output out_55,
  output out_56,
  output out_57,
  output out_58,
  output out_59,
  output out_60
);

  wire and_1_out, and_2_out, and_3_out, and_4_out, and_5_out, and_6_out, and_7_out, and_8_out, and_9_out,
       and_10_out, and_11_out, and_12_out, and_13_out, and_14_out, and_15_out, and_16_out, and_17_out,
       and_18_out, and_19_out, and_20_out, and_21_out, and_22_out, and_23_out, and_25_out, and_26_out,
       and_27_out, and_28_out, and_29_out, and_30_out, and_31_out, and_32_out, and_33_out, and_34_out,
       and_35_out, and_36_out, and_37_out, and_38_out, and_39_out, and_40_out, and_41_out, not_1_out,
       not_2_out, not_3_out, not_4_out, not_5_out, not_6_out, not_7_out, not_8_out, not_9_out, not_10_out,
       not_11_out, not_12_out, not_13_out, not_14_out, not_15_out, not_16_out, not_17_out, not_18_out,
       not_19_out, not_20_out, not_21_out, not_22_out, not_23_out, not_24_out, not_25_out, not_26_out,
       not_27_out, not_28_out, not_29_out, not_30_out, not_31_out, not_32_out, not_33_out, or_4_out,
       or_5_out, or_11_out, or_13_out, or_16_out, or_17_out, or_19_out, or_21_out, or_22_out, or_23_out;

  not not_1 (not_1_out, A);
  not not_2 (not_2_out, C_6);
  and and_1 (and_1_out, not_1_out, C_2);
  and and_2 (and_2_out, C_2, B_3);
  and and_3 (and_3_out, A_6, not_2_out);
  or or_1 (out_52, and_3_out, and_4_out);
  and and_4 (and_4_out, not_2_out, B_7);
  or or_2 (out_47, and_1_out, and_2_out);
  not not_3 (not_3_out, C_7);
  not not_4 (not_4_out, B);
  not not_5 (not_5_out, a_5);
  not not_6 (not_6_out, A_9);
  and and_5 (and_5_out, not_6_out, not_3_out);
  and and_6 (and_6_out, not_3_out, B_9);
  and and_7 (and_7_out, C, A_2);
  or or_3 (out_46, and_7_out, and_8_out);
  and and_8 (and_8_out, A_2, not_4_out);
  and and_9 (and_9_out, not_5_out, c_5);
  and and_10 (and_10_out, c_5, b_5);
  and and_11 (and_11_out, b_5, not_5_out);
  or or_4 (or_4_out, and_5_out, and_6_out);
  and and_12 (and_12_out, B_9, A_9);
  or or_5 (or_5_out, and_9_out, and_10_out);
  or or_6 (out_54, or_4_out, and_12_out);
  or or_7 (out_50, or_5_out, and_11_out);
  not not_7 (not_7_out, A_13);
  not not_8 (not_8_out, C_12);
  not not_9 (not_9_out, B_13);
  not not_10 (not_10_out, C_13);
  not not_11 (not_11_out, B_10);
  not not_12 (not_12_out, C_9);
  not not_13 (not_13_out, C_10);
  not not_14 (not_14_out, B_11);
  and and_13 (and_13_out, not_7_out, not_8_out);
  and and_14 (and_14_out, not_8_out, not_9_out);
  and and_15 (and_15_out, A_14, not_10_out);
  or or_8 (out_60, and_15_out, and_16_out);
  and and_16 (and_16_out, not_10_out, B_14);
  not not_15 (not_15_out, A_3);
  not not_16 (not_16_out, C_3);
  not not_17 (not_17_out, A_7);
  not not_18 (not_18_out, B_6);
  not not_19 (not_19_out, A_8);
  not not_20 (not_20_out, B_8);
  not not_21 (not_21_out, C_8);
  and and_17 (and_17_out, A_10, not_11_out);
  and and_18 (and_18_out, not_11_out, not_12_out);
  and and_19 (and_19_out, not_12_out, A_10);
  and and_20 (and_20_out, A_11, not_13_out);
  or or_9 (out_57, and_20_out, and_21_out);
  and and_21 (and_21_out, not_13_out, not_14_out);
  or or_10 (out_59, and_13_out, and_14_out);
  and and_22 (and_22_out, not_15_out, B_2);
  and and_23 (and_23_out, not_15_out, not_16_out);
  and and_24 (out_51, not_17_out, not_18_out);
  and and_25 (and_25_out, not_19_out, B_8);
  and and_26 (and_26_out, not_20_out, A_8);
  and and_27 (and_27_out, not_19_out, not_21_out);
  or or_11 (or_11_out, and_18_out, and_19_out);
  or or_12 (out_49, and_22_out, and_23_out);
  or or_13 (or_13_out, and_25_out, and_26_out);
  or or_14 (out_53, or_13_out, and_27_out);
  or or_15 (out_56, and_17_out, or_11_out);
  not not_22 (not_22_out, B_12);
  not not_23 (not_23_out, C_11);
  not not_24 (not_24_out, A_12);
  and and_28 (and_28_out, A_12, not_22_out);
  and and_29 (and_29_out, not_22_out, not_23_out);
  not not_25 (not_25_out, B_4);
  or or_16 (or_16_out, and_28_out, and_29_out);
  or or_17 (or_17_out, and_29_out, and_30_out);
  and and_30 (and_30_out, not_23_out, not_24_out);
  and and_31 (and_31_out, A_4, not_25_out);
  and and_32 (and_32_out, not_25_out, not_26_out);
  not not_26 (not_26_out, C_4);
  or or_18 (out_58, or_16_out, or_17_out);
  and and_33 (and_33_out, A_4, not_25_out);
  and and_34 (and_34_out, and_31_out, D);
  and and_35 (and_35_out, C_4, not_25_out);
  and and_36 (and_36_out, and_32_out, D);
  and and_37 (and_37_out, C_4, and_33_out);
  not not_27 (not_27_out, D);
  and and_38 (and_38_out, not_27_out, and_35_out);
  not not_28 (not_28_out, Y);
  not not_29 (not_29_out, X);
  and and_39 (and_39_out, Y, X);
  and and_40 (and_40_out, Z, Y);
  not not_30 (not_30_out, X);
  or or_19 (or_19_out, and_37_out, and_34_out);
  or or_20 (out_48, or_19_out, or_21_out);
  or or_21 (or_21_out, and_38_out, and_36_out);
  not not_31 (not_31_out, or_22_out);
  or or_22 (or_22_out, not_28_out, not_29_out);
  not not_32 (not_32_out, and_39_out);
  not not_33 (not_33_out, or_23_out);
  or or_23 (or_23_out, and_40_out, not_30_out);
  and and_41 (and_41_out, not_31_out, not_32_out);
  or or_24 (out_55, and_41_out, not_33_out);

  // Notes on the sheet:
  //   EX 1B
  //   EX 1A
  //   EX01E
  //   EX 1C
  //   ex 1 D
  //   EX 2 C MINTERMOS
  //   EX 2 D 
  //   EX 2 D
  //   EX 2 B MAXTERMOS
  //   EX 2 B MINTERMOS
  //   EX 2 C MAXTERMOS
  //   EX 2 A
  //   EX 3 A
  //   EX 5
endmodule
