// Logisim project Circuitos.circ as structural Verilog: 1 circuit, main circuit main
module main (
  input  E___0,
  input  E___0_2,
  input  E___1,
  input  E,
  input  E___1_2,
  input  E___2,
  input  A,
  input  E___3,
  input  \Var_Seleção ,
  input  E___0_3,
  input  in_11,
  input  in_12,
  input  E___1_3,
  input  in_14,
  input  E___2_2,
  input  E___3_2,
  input  in_17,
  input  in_18,
  input  in_19,
  input  in_20,
  input  in_21,
  input  E_2,
  input  in_23,
  input  in_24,
  input  in_25,
  input  \Var_Seleção_2 ,
  input  in_27,
  input  in_28,
  input  in_29,
  input  in_30,
  input  in_31,
  input  in_32,
  input  in_33,
  input  A_2,
  input  B,
  input  in_36,
  input  in_37,
  output S___A_prime_E0___A_E1,
  output S___E_A_prime,
  output A__B__S,
  output S___E_A,
  output S___A_prime_B_prime_E0___A_prime_B_E1___A_B_prime_E2___A_B_E3,
  output out_43,
  output S___E_A_prime_2,
  output S___E_A_2,
  output ERRO,
  output out_47,
  output S0___A_prime_B_prime_E,
  output S1___A_prime_B_E,
  output S2___A_B_prime_E,
  output S3___A_B_E
);

  wire and_1_out, and_2_out, and_3_out, and_4_out, and_5_out, and_6_out, and_15_out, and_16_out, and_17_out,
       and_18_out, and_19_out, and_20_out, and_21_out, and_22_out, nand_1_out, nand_2_out, nand_3_out,
       nor_1_out, nor_2_out, nor_3_out, nor_4_out, nor_5_out, nor_6_out, nor_7_out, nor_8_out, nor_9_out,
       nor_10_out, nor_11_out, nor_12_out, nor_13_out, nor_14_out, nor_15_out, nor_16_out, nor_17_out,
       nor_18_out, nor_20_out, nor_21_out, not_1_out, not_2_out, not_3_out, not_4_out, not_5_out, not_6_out,
       not_7_out, not_8_out, not_9_out, not_10_out, not_11_out, not_12_out, not_13_out, not_14_out, or_3_out,
       or_4_out, or_6_out, or_7_out, or_9_out, or_10_out, or_11_out, or_12_out, or_14_out;

  not not_1 (not_1_out, A);
  not not_2 (not_2_out, in_19);
  not not_3 (not_3_out, in_20);
  not not_4 (not_4_out, in_19);
  not not_5 (not_5_out, in_19);
  not not_6 (not_6_out, \Var_Seleção_2 );
  not not_7 (not_7_out, A_2);
  not not_8 (not_8_out, B);
  not not_9 (not_9_out, A_2);
  not not_10 (not_10_out, B);
  and and_1 (and_1_out, E___0, not_1_out);
  and and_2 (and_2_out, E___1, A);
  and and_3 (and_3_out, E___0_3, not_2_out, not_3_out);
  and and_4 (and_4_out, E___1_3, not_4_out, in_20);
  and and_5 (and_5_out, E___2_2, in_20, not_5_out);
  and and_6 (and_6_out, E___3_2, in_19, in_20);
  and and_7 (S___E_A_prime_2, E_2, not_6_out);
  and and_8 (S___E_A_2, \Var_Seleção_2 , E_2);
  and and_9 (S0___A_prime_B_prime_E, in_31, not_7_out, not_8_out);
  and and_10 (S1___A_prime_B_E, in_31, not_9_out, B);
  and and_11 (S2___A_B_prime_E, in_31, A_2, not_10_out);
  and and_12 (S3___A_B_E, in_31, A_2, B);
  or or_1 (S___A_prime_E0___A_E1, and_1_out, and_2_out);
  or or_2 (S___A_prime_B_prime_E0___A_prime_B_E1___A_B_prime_E2___A_B_E3, and_3_out, and_4_out, and_5_out, and_6_out);
  and and_13 (S___E_A_prime, E, nand_1_out);
  nand nand_1 (nand_1_out, \Var_Seleção , \Var_Seleção );
  and and_14 (S___E_A, \Var_Seleção , E);
  nor nor_1 (nor_1_out, in_14, in_14);
  or or_3 (or_3_out, in_21, in_21);
  nor nor_2 (nor_2_out, in_17, in_17);
  nor nor_3 (nor_3_out, in_21, in_21);
  and and_15 (and_15_out, in_23, nand_2_out);
  nand nand_2 (nand_2_out, in_33, in_33);
  and and_16 (and_16_out, in_25, in_33);
  nor nor_4 (nor_4_out, in_28, in_28);
  or or_4 (or_4_out, in_33, in_33);
  nor nor_5 (nor_5_out, in_29, in_29);
  nor nor_6 (nor_6_out, in_33, in_33);
  nor nor_7 (nor_7_out, nor_1_out, or_3_out);
  nor nor_8 (nor_8_out, nor_2_out, nor_3_out);
  nor nor_9 (nor_9_out, nor_4_out, or_4_out);
  nor nor_10 (nor_10_out, nor_5_out, nor_6_out);
  or or_5 (out_43, nor_7_out, nor_8_out);
  or or_6 (or_6_out, and_15_out, and_16_out);
  or or_7 (or_7_out, nor_9_out, nor_10_out);
  and and_17 (and_17_out, or_6_out, nand_3_out);
  nand nand_3 (nand_3_out, in_32, in_32);
  and and_18 (and_18_out, or_7_out, in_32);
  or or_8 (out_47, and_17_out, and_18_out);
  not not_11 (not_11_out, in_11);
  not not_12 (not_12_out, in_12);
  not not_13 (not_13_out, in_11);
  not not_14 (not_14_out, in_11);
  and and_19 (and_19_out, E___0_2, not_11_out, not_12_out);
  and and_20 (and_20_out, E___1_2, not_13_out, in_12);
  and and_21 (and_21_out, E___2, in_12, not_14_out);
  and and_22 (and_22_out, E___3, in_11, in_12);
  nor nor_11 (nor_11_out, in_18, in_18);
  or or_9 (or_9_out, in_36, in_36);
  or or_10 (or_10_out, in_37, in_37);
  nor nor_12 (nor_12_out, in_24, in_24);
  or or_11 (or_11_out, in_36, in_36);
  nor nor_13 (nor_13_out, in_37, in_37);
  nor nor_14 (nor_14_out, in_27, in_27);
  nor nor_15 (nor_15_out, in_36, in_36);
  or or_12 (or_12_out, in_37, in_37);
  nor nor_16 (nor_16_out, in_30, in_30);
  nor nor_17 (nor_17_out, in_36, in_36);
  nor nor_18 (nor_18_out, in_37, in_37);
  or or_13 (A__B__S, and_19_out, and_20_out, and_21_out, and_22_out);
  or or_14 (or_14_out, nor_11_out, or_9_out, or_10_out);
  nor nor_19 (or_14_out, nor_12_out, or_11_out, nor_13_out);
  or or_15 (ERRO, or_14_out, or_14_out, nor_20_out, nor_21_out);
  nor nor_20 (nor_20_out, nor_14_out, nor_15_out, or_12_out);
  nor nor_21 (nor_21_out, nor_16_out, nor_17_out, nor_18_out);

  // Notes on the sheet:
  //   CHAVE SELETORA
  //   MULTIPLEXADOR DE 2 CANAIS
  //   MULTIPLEXADOR DE 4 CANAIS
  //   DEMUX DE 2 SAIDAS
  //   A  B  S
  //   0  0  E0
  //   0  1  E1
  //   1  0  E2
  //   1  1  E3
  //   QUESTÃO 1
  //   QUESTÃO 2
  //   Variável de seleção - portas
  //   sC= (c'+s)'  +  (d'+s')'
  //   s= (a'+s)'  +  (b'+s')'
  //   sA = s'.a + s.b 
  //   QUESTÃO 3
  //   Variável de seleção - grupo AND ou OR
  //   s = s1'.(s'.a + s.b) + s1.((c'+s)'  +  (d'+s')')
  //   s = s'.sA + s.sC
  //   s= (a'+s)'  +  (b'+s')'
  //   MULTIPLEXADOR DE 4 CANAIS
  //   0  0  E0
  //   0  1  E1
  //   1  0  E2
  //   1  1  E3
endmodule
