// Logisim project Circuitos.circ as structural Verilog
module EX01 (
  input  [4:0] a,
  input  [4:0] b,
  output Carry_in,
  output [4:0] s
);

  wire full_adder_com_half_sum_1_out_4, full_adder_com_half_sum_2_out_4, full_adder_com_half_sum_4_out_4,
       half_sum_1_s1;

  Half_sum half_sum_1 (.a(b[0]), .b(a[0]), .S1(half_sum_1_s1), .S0(s[0]));
  Full_adder_com_half_sum full_adder_com_half_sum_1 (
    .in_1(a[2]), .in_2(b[2]), .in_3(full_adder_com_half_sum_2_out_4),
    .out_4(full_adder_com_half_sum_1_out_4), .out_5(s[2]));
  Full_adder_com_half_sum full_adder_com_half_sum_2 (
    .in_1(b[1]), .in_2(a[1]), .in_3(half_sum_1_s1), .out_4(full_adder_com_half_sum_2_out_4), .out_5(s[1]));
  Full_adder_com_half_sum full_adder_com_half_sum_3 (
    .in_1(a[4]), .in_2(b[4]), .in_3(full_adder_com_half_sum_4_out_4), .out_4(Carry_in), .out_5(s[4]));
  Full_adder_com_half_sum full_adder_com_half_sum_4 (
    .in_1(a[3]), .in_2(b[3]), .in_3(full_adder_com_half_sum_1_out_4),
    .out_4(full_adder_com_half_sum_4_out_4), .out_5(s[3]));
endmodule

module Full_adder_com_half_sum (
  input  in_1,
  input  in_2,
  input  in_3,
  output out_4,
  output out_5
);

  wire half_sum_1_s0, half_sum_1_s1, half_sum_2_s1;

  Half_sum half_sum_1 (.a(in_1), .b(in_2), .S1(half_sum_1_s1), .S0(half_sum_1_s0));
  Half_sum half_sum_2 (.a(half_sum_1_s0), .b(in_3), .S1(half_sum_2_s1), .S0(out_5));
  Half_sum half_sum_3 (.a(half_sum_1_s1), .b(half_sum_2_s1), .S0(out_4));  // open: S1
endmodule

module Half_sum (
  input  a,
  input  b,
  output S1,
  output S0
);

  wire and_1_out, and_2_out, not_1_out, not_2_out;

  not not_1 (not_1_out, a);
  not not_2 (not_2_out, b);
  and and_1 (and_1_out, not_1_out, b);
  and and_2 (and_2_out, not_2_out, a);
  and and_3 (S1, a, b);
  or or_1 (S0, and_1_out, and_2_out);
endmodule

module Ex01 (
  input  [4:0] a,
  input  [4:0] b,
  output Carry_in,
  output [4:0] s
);

  wire full_adder_com_half_sum_1_out_4, full_adder_com_half_sum_2_out_4, full_adder_com_half_sum_3_out_4,
       half_sum_1_s1;

  Full_adder_com_half_sum full_adder_com_half_sum_1 (
    .in_1(b[1]), .in_2(a[1]), .in_3(half_sum_1_s1), .out_4(full_adder_com_half_sum_1_out_4), .out_5(s[1]));
  Half_sum half_sum_1 (.a(b[0]), .b(a[0]), .S1(half_sum_1_s1), .S0(s[0]));
  Full_adder_com_half_sum full_adder_com_half_sum_2 (
    .in_1(a[3]), .in_2(b[3]), .in_3(full_adder_com_half_sum_3_out_4),
    .out_4(full_adder_com_half_sum_2_out_4), .out_5(s[3]));
  Full_adder_com_half_sum full_adder_com_half_sum_3 (
    .in_1(a[2]), .in_2(b[2]), .in_3(full_adder_com_half_sum_1_out_4),
    .out_4(full_adder_com_half_sum_3_out_4), .out_5(s[2]));
  Full_adder_com_half_sum full_adder_com_half_sum_4 (
    .in_1(a[4]), .in_2(b[4]), .in_3(full_adder_com_half_sum_2_out_4), .out_4(Carry_in), .out_5(s[4]));
endmodule

module Full_adder_com_half_sum_PORTAS_NATIVAS (
  input  a,
  input  b,
  input  c,
  output x,
  output y
);

  wire nand_1_out, nand_2_out, nand_3_out, nand_4_out, nand_5_out, nand_6_out, nand_7_out, nand_8_out,
       nand_9_out, nand_11_out, nand_12_out, nand_13_out, nand_14_out;

  nand nand_1 (nand_1_out, b, c);
  nand nand_2 (nand_2_out, a, c);
  nand nand_3 (nand_3_out, a, b);
  nand nand_4 (nand_4_out, a, a);
  nand nand_5 (nand_5_out, b, b);
  nand nand_6 (nand_6_out, a, a);
  nand nand_7 (nand_7_out, c, c);
  nand nand_8 (nand_8_out, b, b);
  nand nand_9 (nand_9_out, c, c);
  nand nand_10 (x, nand_1_out, nand_2_out, nand_3_out);
  nand nand_11 (nand_11_out, nand_4_out, nand_5_out, c);
  nand nand_12 (nand_12_out, nand_6_out, b, nand_7_out);
  nand nand_13 (nand_13_out, a, nand_8_out, nand_9_out);
  nand nand_14 (nand_14_out, a, b, c);
  nand nand_15 (y, nand_11_out, nand_12_out, nand_13_out, nand_14_out);
endmodule

module Half_Sub (
  input  a,
  input  b,
  output sinal,
  output amplitude
);

  wire and_2_out, not_1_out, not_2_out;

  not not_1 (not_1_out, a);
  not not_2 (not_2_out, b);
  and and_1 (sinal, not_1_out, b);
  and and_2 (and_2_out, a, not_2_out);
  or or_1 (amplitude, sinal, and_2_out);
endmodule

module Full_sub (
  input  in_1,
  input  b,
  input  c,
  output sinal,
  output amplitude
);

  wire half_sub_1_amplitude, half_sub_1_sinal, half_sub_2_sinal;

  Half_Sub half_sub_1 (.a(in_1), .b(b), .sinal(half_sub_1_sinal), .amplitude(half_sub_1_amplitude));
  Half_Sub half_sub_2 (.a(half_sub_1_amplitude), .b(c), .sinal(half_sub_2_sinal), .amplitude(amplitude));
  or or_1 (sinal, half_sub_1_sinal, half_sub_2_sinal);
endmodule

module Full_sub_PORTAS_NATIVAS (
  input  a,
  input  b,
  input  c,
  output sinal,
  output amplitude
);

  wire nand_1_out, nand_2_out, nand_3_out, nand_4_out, nand_5_out, nand_6_out, nand_7_out, nand_8_out,
       nand_9_out, nand_10_out, nand_11_out, nand_12_out, nand_13_out, nand_14_out, nand_15_out;

  nand nand_1 (nand_1_out, a, a);
  nand nand_2 (nand_2_out, a, a);
  nand nand_3 (nand_3_out, a, a);
  nand nand_4 (nand_4_out, b, b);
  nand nand_5 (nand_5_out, a, a);
  nand nand_6 (nand_6_out, c, c);
  nand nand_7 (nand_7_out, b, b);
  nand nand_8 (nand_8_out, c, c);
  nand nand_9 (nand_9_out, nand_1_out, c);
  nand nand_10 (nand_10_out, nand_2_out, b);
  nand nand_11 (nand_11_out, b, c);
  nand nand_12 (nand_12_out, nand_3_out, nand_4_out, c);
  nand nand_13 (nand_13_out, nand_5_out, b, nand_6_out);
  nand nand_14 (nand_14_out, a, nand_7_out, nand_8_out);
  nand nand_15 (nand_15_out, a, b, c);
  nand nand_16 (sinal, nand_9_out, nand_10_out, nand_11_out);
  nand nand_17 (amplitude, nand_12_out, nand_13_out, nand_14_out, nand_15_out);
endmodule

module EX02 (
  input  [4:0] a,
  input  [4:0] b,
  output Carry_in,
  output [4:0] s
);

  wire full_adder_com_half_sum_1_out_4, full_adder_com_half_sum_2_out_4, full_adder_com_half_sum_4_out_4,
       half_sum_1_s1;

  Half_sum half_sum_1 (.a(b[0]), .b(a[0]), .S1(half_sum_1_s1), .S0(s[0]));
  Full_adder_com_half_sum full_adder_com_half_sum_1 (
    .in_1(a[2]), .in_2(b[2]), .in_3(full_adder_com_half_sum_2_out_4),
    .out_4(full_adder_com_half_sum_1_out_4), .out_5(s[2]));
  Full_adder_com_half_sum full_adder_com_half_sum_2 (
    .in_1(b[1]), .in_2(a[1]), .in_3(half_sum_1_s1), .out_4(full_adder_com_half_sum_2_out_4), .out_5(s[1]));
  Full_adder_com_half_sum full_adder_com_half_sum_3 (
    .in_1(a[4]), .in_2(b[4]), .in_3(full_adder_com_half_sum_4_out_4), .out_4(Carry_in), .out_5(s[4]));
  Full_adder_com_half_sum full_adder_com_half_sum_4 (
    .in_1(a[3]), .in_2(b[3]), .in_3(full_adder_com_half_sum_1_out_4),
    .out_4(full_adder_com_half_sum_4_out_4), .out_5(s[3]));
endmodule

module EX03 (
  input  [4:0] in_1,
  input  [4:0] in_2,
  output out_3
);

  wire ex02_1_carry_in, or_1_out;
  wire [4:0] ex02_1_s;

  EX02 ex02_1 (.a(in_1), .b(in_2), .Carry_in(ex02_1_carry_in), .s(ex02_1_s));
  not not_1 (out_3, or_1_out);
  or or_1 (or_1_out, ex02_1_carry_in, ex02_1_s[0], ex02_1_s[1], ex02_1_s[2], ex02_1_s[3], ex02_1_s[4]);
endmodule

module EX04 (
  input  [4:0] a,
  input  [4:0] b,
  output out_3,
  output out_4,
  output out_5
);

  wire ex02_1_carry_in, not_2_out, or_1_out;
  wire [4:0] ex02_1_s;

  EX02 ex02_1 (.a(a), .b(b), .Carry_in(ex02_1_carry_in), .s(ex02_1_s));
  and and_1 (out_3, ex02_1_carry_in, or_1_out);
  not not_1 (out_4, or_1_out);
  or or_1 (or_1_out, ex02_1_carry_in, ex02_1_s[0], ex02_1_s[1], ex02_1_s[2], ex02_1_s[3], ex02_1_s[4]);
  not not_2 (not_2_out, ex02_1_carry_in);
  and and_2 (out_5, or_1_out, not_2_out);
endmodule

module EX05 (
  input  in_1,
  input  in_2,
  input  [4:0] a,
  output [4:0] out_4
);

  wire [4:0] complemento_de_1_1_complemento;

  Complemento_de_1 complemento_de_1_1 (.a(a), .Complemento(complemento_de_1_1_complemento));
  Ex01 ex01_1 (.a(complemento_de_1_1_complemento), .b({{4{in_1}}, in_2}), .s(out_4));  // open: Carry_in
endmodule

module Complemento_de_1 (
  input  [4:0] a,
  output [4:0] Complemento
);

  assign Complemento = ~a;  // NOT_Gate not_1, 5 bits wide
endmodule
