// Logisim project circuitos.circ as structural Verilog: 9 circuits, main circuit 1x1 
// 1x1
module _1x1 (
  input  R_W,
  input  Address,
  input  Clock,
  input  Clear,
  input  Input,
  output Output
);

  wire and_1_out, d_ff_1_q;

  and and_1 (and_1_out, Address, R_W, Clock);
  D_Flip_Flop d_ff_1 (.clk(and_1_out), .D(Input), .Q(d_ff_1_q), .reset(Clear));  // open: Qn, preset
  and and_2 (Output, Address, d_ff_1_q);
endmodule

module _1x2 (
  input  R_W,
  input  Address,
  input  CLK,
  input  CLR,
  input  [1:0] Input,
  output [1:0] Output
);

  _1x1 u_1x1_1 (.R_W(R_W), .Clock(CLK), .Clear(CLR), .Address(Address), .Output(Output[1]), .Input(Input[1]));
  _1x1 u_1x1_2 (.R_W(R_W), .Clock(CLK), .Clear(CLR), .Address(Address), .Output(Output[0]), .Input(Input[0]));
endmodule

module _1x4 (
  input  Address,
  input  R_W,
  input  CLK,
  input  Clear,
  input  [3:0] Input,
  output [3:0] Output
);

  _1x2 u_1x2_1 (.R_W(R_W), .CLK(CLK), .CLR(Clear), .Address(Address), .Output(Output[3:2]), .Input(Input[3:2]));
  _1x2 u_1x2_2 (.R_W(R_W), .CLK(CLK), .CLR(Clear), .Address(Address), .Output(Output[1:0]), .Input(Input[1:0]));
endmodule

module _2x4 (
  input  Address,
  input  R_W,
  input  [3:0] Input,
  input  CLK,
  input  Clear,
  output [3:0] Output
);

  wire demultiplexer_1_out0, demultiplexer_1_out1;
  wire [3:0] n1x4_1_output, n1x4_2_output;

  Demultiplexer #(.enable("false")) demultiplexer_1 (
    .out0(demultiplexer_1_out0), .out1(demultiplexer_1_out1), .in(1'b1), .sel(Address));
  _1x4 u_1x4_1 (
    .R_W(R_W), .CLK(CLK), .Clear(Clear), .Address(demultiplexer_1_out0), .Output(n1x4_1_output), .Input(Input));
  _1x4 u_1x4_2 (
    .R_W(R_W), .CLK(CLK), .Clear(Clear), .Address(demultiplexer_1_out1), .Output(n1x4_2_output), .Input(Input));
  Multiplexer #(.width(4), .enable("false")) multiplexer_1 (
    .in0(n1x4_1_output), .in1(n1x4_2_output), .out(Output), .sel(Address));
endmodule

module _4x4 (
  input  [1:0] Address,
  input  R_W,
  input  CLK,
  input  [3:0] Input,
  input  CLR,
  output [3:0] Output
);

  wire demultiplexer_1_out0, demultiplexer_1_out1, demultiplexer_1_out2, demultiplexer_1_out3;
  wire [3:0] n1x4_1_output, n1x4_2_output, n1x4_3_output, n1x4_4_output;

  Demultiplexer #(.select(2), .enable("false")) demultiplexer_1 (
    .out0(demultiplexer_1_out0), .out1(demultiplexer_1_out1), .out2(demultiplexer_1_out2),
    .out3(demultiplexer_1_out3), .in(1'b1), .sel(Address));
  _1x4 u_1x4_1 (
    .R_W(R_W), .CLK(CLK), .Clear(CLR), .Address(demultiplexer_1_out0), .Output(n1x4_1_output), .Input(Input));
  _1x4 u_1x4_2 (
    .R_W(R_W), .CLK(CLK), .Clear(CLR), .Address(demultiplexer_1_out1), .Output(n1x4_2_output), .Input(Input));
  _1x4 u_1x4_3 (
    .R_W(R_W), .CLK(CLK), .Clear(CLR), .Address(demultiplexer_1_out2), .Output(n1x4_3_output), .Input(Input));
  _1x4 u_1x4_4 (
    .R_W(R_W), .CLK(CLK), .Clear(CLR), .Address(demultiplexer_1_out3), .Output(n1x4_4_output), .Input(Input));
  Multiplexer #(.select(2), .width(4), .enable("false")) multiplexer_1 (
    .in0(n1x4_1_output), .in1(n1x4_2_output), .in2(n1x4_3_output), .in3(n1x4_4_output), .out(Output),
    .sel(Address));
endmodule

module _8x8 (
  input  [2:0] in_1,
  input  [7:0] in_2,
  input  R_W,
  input  CLK,
  input  Clear,
  output [7:0] out_6
);

  wire demultiplexer_1_out0, demultiplexer_1_out1, demultiplexer_1_out2, demultiplexer_1_out3,
       demultiplexer_1_out4, demultiplexer_1_out5, demultiplexer_1_out6, demultiplexer_1_out7;
  wire [7:0] n1x8_1_output, n1x8_2_output, n1x8_3_output, n1x8_4_output, n1x8_5_output, n1x8_6_output,
       n1x8_7_output, n1x8_8_output;

  Demultiplexer #(.select(3), .enable("false")) demultiplexer_1 (
    .out0(demultiplexer_1_out0), .out1(demultiplexer_1_out1), .out2(demultiplexer_1_out2),
    .out3(demultiplexer_1_out3), .out4(demultiplexer_1_out4), .out5(demultiplexer_1_out5),
    .out6(demultiplexer_1_out6), .out7(demultiplexer_1_out7), .in(1'b1), .sel(in_1));
  _1x8 u_1x8_1 (
    .R_w(R_W), .CLK(CLK), .Clear(Clear), .Address(demultiplexer_1_out0), .Output(n1x8_1_output), .Input(in_2));
  _1x8 u_1x8_2 (
    .R_w(R_W), .CLK(CLK), .Clear(Clear), .Address(demultiplexer_1_out1), .Output(n1x8_2_output), .Input(in_2));
  _1x8 u_1x8_3 (
    .R_w(R_W), .CLK(CLK), .Clear(Clear), .Address(demultiplexer_1_out2), .Output(n1x8_3_output), .Input(in_2));
  _1x8 u_1x8_4 (
    .R_w(R_W), .CLK(CLK), .Clear(Clear), .Address(demultiplexer_1_out3), .Output(n1x8_4_output), .Input(in_2));
  _1x8 u_1x8_5 (
    .R_w(R_W), .CLK(CLK), .Clear(Clear), .Address(demultiplexer_1_out4), .Output(n1x8_5_output), .Input(in_2));
  _1x8 u_1x8_6 (
    .R_w(R_W), .CLK(CLK), .Clear(Clear), .Address(demultiplexer_1_out5), .Output(n1x8_6_output), .Input(in_2));
  _1x8 u_1x8_7 (
    .R_w(R_W), .CLK(CLK), .Clear(Clear), .Address(demultiplexer_1_out6), .Output(n1x8_7_output), .Input(in_2));
  _1x8 u_1x8_8 (
    .R_w(R_W), .CLK(CLK), .Clear(Clear), .Address(demultiplexer_1_out7), .Output(n1x8_8_output), .Input(in_2));
  Multiplexer #(.select(3), .width(8), .enable("false")) multiplexer_1 (
    .in0(n1x8_1_output), .in1(n1x8_2_output), .in2(n1x8_3_output), .in3(n1x8_4_output), .in4(n1x8_5_output),
    .in5(n1x8_6_output), .in6(n1x8_7_output), .in7(n1x8_8_output), .out(out_6), .sel(in_1));
endmodule

module _1x8 (
  input  R_w,
  input  CLK,
  input  Address,
  input  Clear,
  input  [7:0] Input,
  output [7:0] Output
);

  _1x1 u_1x1_1 (.R_W(R_w), .Clock(CLK), .Clear(Clear), .Address(Address), .Output(Output[7]), .Input(Input[7]));
  _1x1 u_1x1_2 (.R_W(R_w), .Clock(CLK), .Clear(Clear), .Address(Address), .Output(Output[6]), .Input(Input[6]));
  _1x1 u_1x1_3 (.R_W(R_w), .Clock(CLK), .Clear(Clear), .Address(Address), .Output(Output[5]), .Input(Input[5]));
  _1x1 u_1x1_4 (.R_W(R_w), .Clock(CLK), .Clear(Clear), .Address(Address), .Output(Output[4]), .Input(Input[4]));
  _1x1 u_1x1_5 (.R_W(R_w), .Clock(CLK), .Clear(Clear), .Address(Address), .Output(Output[3]), .Input(Input[3]));
  _1x1 u_1x1_6 (.R_W(R_w), .Clock(CLK), .Clear(Clear), .Address(Address), .Output(Output[2]), .Input(Input[2]));
  _1x1 u_1x1_7 (.R_W(R_w), .Clock(CLK), .Clear(Clear), .Address(Address), .Output(Output[1]), .Input(Input[1]));
  _1x1 u_1x1_8 (.R_W(R_w), .Clock(CLK), .Clear(Clear), .Address(Address), .Output(Output[0]), .Input(Input[0]));
endmodule

module _4x8 (
  input  [1:0] Address,
  input  R_W,
  input  CLK,
  input  [7:0] Input,
  input  CLR,
  output [7:0] Output
);

  wire demultiplexer_1_out0, demultiplexer_1_out1, demultiplexer_1_out2, demultiplexer_1_out3;
  wire [7:0] n1x8_1_output, n1x8_2_output, n1x8_3_output, n1x8_4_output;

  Demultiplexer #(.select(2), .enable("false")) demultiplexer_1 (
    .out0(demultiplexer_1_out0), .out1(demultiplexer_1_out1), .out2(demultiplexer_1_out2),
    .out3(demultiplexer_1_out3), .in(1'b1), .sel(Address));
  _1x8 u_1x8_1 (
    .R_w(R_W), .CLK(CLK), .Clear(CLR), .Address(demultiplexer_1_out0), .Output(n1x8_1_output), .Input(Input));
  _1x8 u_1x8_2 (
    .R_w(R_W), .CLK(CLK), .Clear(CLR), .Address(demultiplexer_1_out1), .Output(n1x8_2_output), .Input(Input));
  _1x8 u_1x8_3 (
    .R_w(R_W), .CLK(CLK), .Clear(CLR), .Address(demultiplexer_1_out2), .Output(n1x8_3_output), .Input(Input));
  _1x8 u_1x8_4 (
    .R_w(R_W), .CLK(CLK), .Clear(CLR), .Address(demultiplexer_1_out3), .Output(n1x8_4_output), .Input(Input));
  Multiplexer #(.select(2), .width(8), .enable("false")) multiplexer_1 (
    .in0(n1x8_1_output), .in1(n1x8_2_output), .in2(n1x8_3_output), .in3(n1x8_4_output), .out(Output),
    .sel(Address));
endmodule

module _8x8__usando_4x8 (
  input  Address,
  input  R_W,
  input  [7:0] Input,
  input  CLK,
  input  Clear,
  output [7:0] Output
);

  wire [1:0] demultiplexer_1_out0, demultiplexer_1_out1;
  wire [7:0] undriven, undriven_2;

  Demultiplexer #(.width(2), .enable("false")) demultiplexer_1 (
    .out0(demultiplexer_1_out0), .out1(demultiplexer_1_out1), .in(2'b11), .sel(Address));
  _4x8 u_4x8_1 (.R_W(R_W), .CLK(CLK), .CLR(Clear), .Address(demultiplexer_1_out0), .Input(undriven), .Output(Input));
  _4x8 u_4x8_2 (.R_W(R_W), .CLK(CLK), .CLR(Clear), .Address(demultiplexer_1_out1), .Input(undriven_2), .Output(Input));
  Multiplexer #(.width(8), .enable("false")) multiplexer_1 (
    .in0(undriven), .in1(undriven_2), .out(Output), .sel(Address));
endmodule
