// Logisim project Circuitos.circ as structural Verilog: 5 circuits, main circuit contador_decrescente
module contador_decrescente (
  input  pulse,
  input  in_2,
  input  clear,
  input  in_4,
  input  in_5,
  input  in_6,
  input  in_7,
  input  in_8,
  output out_9,
  output out_10,
  output out_11,
  output out_12,
  output out_13,
  output out_14,
  output out_15,
  output out_16
);

  J_K_Flip_Flop #(.Pre_Clr_Positions("LEGACY"), .NewFFLayout("false")) j_k_ff_1 (
    .J(in_2), .clk(out_10), .K(in_2), .Qn(out_9), .reset(clear));  // open: Q, preset
  J_K_Flip_Flop #(.Pre_Clr_Positions("LEGACY"), .NewFFLayout("false")) j_k_ff_2 (
    .J(in_2), .clk(out_11), .K(in_2), .Qn(out_10), .reset(clear));  // open: Q, preset
  J_K_Flip_Flop j_k_ff_3 (.J(in_6), .clk(in_5), .K(in_7), .Q(out_15), .Qn(out_16), .preset(in_4), .reset(in_8));
  J_K_Flip_Flop #(.Pre_Clr_Positions("LEGACY"), .NewFFLayout("false")) j_k_ff_4 (
    .J(in_2), .clk(out_12), .K(in_2), .Qn(out_11), .reset(clear));  // open: Q, preset
  J_K_Flip_Flop #(.Pre_Clr_Positions("LEGACY"), .NewFFLayout("false")) j_k_ff_5 (
    .J(in_2), .clk(out_13), .K(in_2), .Qn(out_12), .reset(clear));  // open: Q, preset
  J_K_Flip_Flop #(.Pre_Clr_Positions("LEGACY"), .NewFFLayout("false")) j_k_ff_6 (
    .J(in_2), .clk(out_14), .K(in_2), .Qn(out_13), .reset(clear));  // open: Q, preset
  J_K_Flip_Flop #(.Pre_Clr_Positions("LEGACY"), .NewFFLayout("false")) j_k_ff_7 (
    .J(in_2), .clk(pulse), .K(in_2), .Qn(out_14), .reset(clear));  // open: Q, preset
endmodule

module contador_crescente (
  input  pulse,
  input  in_2,
  input  clear,
  output out_4,
  output out_5,
  output out_6,
  output out_7,
  output out_8,
  output out_9
);

  wire j_k_ff_2_qn, j_k_ff_3_qn, j_k_ff_4_qn, j_k_ff_5_qn, j_k_ff_6_qn;

  J_K_Flip_Flop #(.Pre_Clr_Positions("LEGACY"), .NewFFLayout("false")) j_k_ff_1 (
    .J(in_2), .clk(j_k_ff_2_qn), .K(in_2), .Q(out_4), .reset(clear));  // open: Qn, preset
  J_K_Flip_Flop #(.Pre_Clr_Positions("LEGACY"), .NewFFLayout("false")) j_k_ff_2 (
    .J(in_2), .clk(j_k_ff_3_qn), .K(in_2), .Q(out_5), .Qn(j_k_ff_2_qn), .reset(clear));  // open: preset
  J_K_Flip_Flop #(.Pre_Clr_Positions("LEGACY"), .NewFFLayout("false")) j_k_ff_3 (
    .J(in_2), .clk(j_k_ff_4_qn), .K(in_2), .Q(out_6), .Qn(j_k_ff_3_qn), .reset(clear));  // open: preset
  J_K_Flip_Flop #(.Pre_Clr_Positions("LEGACY"), .NewFFLayout("false")) j_k_ff_4 (
    .J(in_2), .clk(j_k_ff_5_qn), .K(in_2), .Q(out_7), .Qn(j_k_ff_4_qn), .reset(clear));  // open: preset
  J_K_Flip_Flop #(.Pre_Clr_Positions("LEGACY"), .NewFFLayout("false")) j_k_ff_5 (
    .J(in_2), .clk(j_k_ff_6_qn), .K(in_2), .Q(out_8), .Qn(j_k_ff_5_qn), .reset(clear));  // open: preset
  J_K_Flip_Flop #(.Pre_Clr_Positions("LEGACY"), .NewFFLayout("false")) j_k_ff_6 (
    .J(in_2), .clk(pulse), .K(in_2), .Q(out_9), .Qn(j_k_ff_6_qn), .reset(clear));  // open: preset
endmodule

module \decádico_decrescente  (
  input  in_1,
  input  pulse,
  output out_3,
  output out_4,
  output out_5,
  output out_6,
  output out_7
);

  wire and_1_out, j_k_ff_2_qn, j_k_ff_4_qn, not_1_out, or_1_out;

  not not_1 (not_1_out, in_1);
  J_K_Flip_Flop j_k_ff_1 (.J(in_1), .clk(pulse), .K(in_1), .Q(out_7), .preset(or_1_out));  // open: Qn, reset
  or or_1 (or_1_out, not_1_out, and_1_out);
  and and_1 (and_1_out, out_7, j_k_ff_2_qn, out_3, out_5, j_k_ff_4_qn);
  J_K_Flip_Flop j_k_ff_2 (
    .J(in_1), .clk(out_7), .K(in_1), .Q(out_6), .Qn(j_k_ff_2_qn), .preset(or_1_out));  // open: reset
  J_K_Flip_Flop j_k_ff_3 (.J(in_1), .clk(out_6), .K(in_1), .Q(out_5), .preset(or_1_out));  // open: Qn, reset
  J_K_Flip_Flop j_k_ff_4 (
    .J(in_1), .clk(out_5), .K(in_1), .Q(out_4), .Qn(j_k_ff_4_qn), .preset(or_1_out));  // open: reset
  J_K_Flip_Flop j_k_ff_5 (.J(in_1), .clk(out_4), .K(in_1), .Q(out_3));  // open: Qn, preset, reset
endmodule

module \decádico_crescente  (
  input  in_1,
  input  pulse,
  output out_3,
  output out_4,
  output out_5,
  output out_6,
  output out_7
);

  wire and_1_out, j_k_ff_1_q, j_k_ff_2_q, j_k_ff_3_q, j_k_ff_4_q, j_k_ff_5_q, not_1_out, or_1_out;

  not not_1 (not_1_out, in_1);
  J_K_Flip_Flop j_k_ff_1 (
    .J(in_1), .clk(pulse), .K(in_1), .Q(j_k_ff_1_q), .Qn(out_7), .preset(or_1_out));  // open: reset
  or or_1 (or_1_out, not_1_out, and_1_out);
  and and_1 (and_1_out, j_k_ff_1_q, out_6, j_k_ff_5_q, j_k_ff_3_q, out_4);
  J_K_Flip_Flop j_k_ff_2 (
    .J(in_1), .clk(j_k_ff_1_q), .K(in_1), .Q(j_k_ff_2_q), .Qn(out_6), .preset(or_1_out));  // open: reset
  J_K_Flip_Flop j_k_ff_3 (
    .J(in_1), .clk(j_k_ff_2_q), .K(in_1), .Q(j_k_ff_3_q), .Qn(out_5), .preset(or_1_out));  // open: reset
  J_K_Flip_Flop j_k_ff_4 (
    .J(in_1), .clk(j_k_ff_3_q), .K(in_1), .Q(j_k_ff_4_q), .Qn(out_4), .preset(or_1_out));  // open: reset
  J_K_Flip_Flop j_k_ff_5 (.J(in_1), .clk(j_k_ff_4_q), .K(in_1), .Q(j_k_ff_5_q), .Qn(out_3));  // open: preset, reset
endmodule

module contador_anel (
  input  in_1,
  input  in_2,
  input  in_3,
  input  in_4,
  input  in_5,
  input  in_6,
  output out_7,
  output out_8,
  output out_9,
  output out_10,
  output out_11,
  output out_12
);

  wire or_1_out, or_2_out;

  or or_1 (or_1_out, out_9, in_2);
  or or_2 (or_2_out, out_12, in_5);
  D_Flip_Flop d_ff_1 (.clk(in_1), .D(or_1_out), .Q(out_7), .reset(in_3));  // open: Qn, preset
  J_K_Flip_Flop j_k_ff_1 (.J(or_2_out), .clk(in_4), .K(or_2_out), .Q(out_10), .reset(in_6));  // open: Qn, preset
  J_K_Flip_Flop j_k_ff_2 (.J(out_10), .clk(in_4), .K(out_10), .Q(out_11), .reset(in_6));  // open: Qn, preset
  D_Flip_Flop d_ff_2 (.clk(in_1), .D(out_7), .Q(out_8), .reset(in_3));  // open: Qn, preset
  D_Flip_Flop d_ff_3 (.clk(in_1), .D(out_8), .Q(out_9), .reset(in_3));  // open: Qn, preset
  J_K_Flip_Flop j_k_ff_3 (.J(out_11), .clk(in_4), .K(out_11), .Q(out_12), .reset(in_6));  // open: Qn, preset
endmodule
