// Logisim project circ.circ as structural Verilog: 4 circuits, main circuit ex01
module ex01 (
  input  clock,
  input  \input ,
  input  clear
);

  wire d_ff_1_q, d_ff_2_q, d_ff_3_q, d_ff_4_q, d_ff_5_q, d_ff_6_q;

  // Probe on d_ff_1_q
  D_Flip_Flop d_ff_1 (.clk(clock), .D(d_ff_2_q), .Q(d_ff_1_q), .reset(clear));  // open: Qn, preset
  // Probe on d_ff_2_q
  D_Flip_Flop d_ff_2 (.clk(clock), .D(d_ff_3_q), .Q(d_ff_2_q), .reset(clear));  // open: Qn, preset
  // Probe on d_ff_3_q
  D_Flip_Flop d_ff_3 (.clk(clock), .D(d_ff_4_q), .Q(d_ff_3_q), .reset(clear));  // open: Qn, preset
  // Probe on d_ff_4_q
  D_Flip_Flop d_ff_4 (.clk(clock), .D(d_ff_5_q), .Q(d_ff_4_q), .reset(clear));  // open: Qn, preset
  // Probe on d_ff_5_q
  D_Flip_Flop d_ff_5 (.clk(clock), .D(d_ff_6_q), .Q(d_ff_5_q), .reset(clear));  // open: Qn, preset
  // Probe on d_ff_6_q
  D_Flip_Flop d_ff_6 (.clk(clock), .D(\input ), .Q(d_ff_6_q), .reset(clear));  // open: Qn, preset
endmodule

module ex03 (
  input  clock,
  input  \input ,
  input  clear
);

  wire d_ff_1_q, d_ff_2_q, d_ff_3_q, d_ff_4_q, d_ff_5_q, d_ff_6_q, or_1_out;

  or or_1 (or_1_out, d_ff_6_q, \input );
  D_Flip_Flop d_ff_1 (.clk(clock), .D(or_1_out), .Q(d_ff_1_q), .reset(clear));  // open: Qn, preset
  // Probe on d_ff_1_q
  // Probe on d_ff_2_q
  D_Flip_Flop d_ff_2 (.clk(clock), .D(d_ff_1_q), .Q(d_ff_2_q), .reset(clear));  // open: Qn, preset
  D_Flip_Flop d_ff_3 (.clk(clock), .D(d_ff_2_q), .Q(d_ff_3_q), .reset(clear));  // open: Qn, preset
  // Probe on d_ff_3_q
  // Probe on d_ff_4_q
  D_Flip_Flop d_ff_4 (.clk(clock), .D(d_ff_3_q), .Q(d_ff_4_q), .reset(clear));  // open: Qn, preset
  // Probe on d_ff_5_q
  D_Flip_Flop d_ff_5 (.clk(clock), .D(d_ff_4_q), .Q(d_ff_5_q), .reset(clear));  // open: Qn, preset
  // Probe on d_ff_6_q
  D_Flip_Flop d_ff_6 (.clk(clock), .D(d_ff_5_q), .Q(d_ff_6_q), .reset(clear));  // open: Qn, preset
endmodule

module ex04 (
  input  clock,
  input  \input ,
  input  clear
);

  wire d_ff_1_q, d_ff_1_qn, d_ff_2_q, d_ff_3_q, d_ff_4_q, d_ff_5_q, d_ff_6_q, or_1_out;

  // Probe on d_ff_1_q
  D_Flip_Flop d_ff_1 (.clk(clock), .D(d_ff_2_q), .Q(d_ff_1_q), .Qn(d_ff_1_qn), .reset(clear));  // open: preset
  or or_1 (or_1_out, d_ff_1_qn, \input );
  // Probe on d_ff_2_q
  D_Flip_Flop d_ff_2 (.clk(clock), .D(d_ff_3_q), .Q(d_ff_2_q), .reset(clear));  // open: Qn, preset
  // Probe on d_ff_3_q
  D_Flip_Flop d_ff_3 (.clk(clock), .D(d_ff_4_q), .Q(d_ff_3_q), .reset(clear));  // open: Qn, preset
  // Probe on d_ff_4_q
  D_Flip_Flop d_ff_4 (.clk(clock), .D(d_ff_5_q), .Q(d_ff_4_q), .reset(clear));  // open: Qn, preset
  // Probe on d_ff_5_q
  D_Flip_Flop d_ff_5 (.clk(clock), .D(d_ff_6_q), .Q(d_ff_5_q), .reset(clear));  // open: Qn, preset
  // Probe on d_ff_6_q
  D_Flip_Flop d_ff_6 (.clk(clock), .D(or_1_out), .Q(d_ff_6_q), .reset(clear));  // open: Qn, preset
endmodule

module ex05 (
  input  in_1,
  input  in_2,
  input  in_3,
  input  in_4,
  input  in_5,
  input  in_6,
  input  ld,
  input  clock,
  input  clear,
  output out_10,
  output out_11,
  output out_12,
  output out_13,
  output out_14,
  output out_15
);

  wire and_1_out, and_2_out, and_3_out, and_4_out, and_5_out, and_6_out;

  and and_1 (and_1_out, ld, in_1);
  D_Flip_Flop d_ff_1 (.clk(clock), .D(1'b0), .Q(out_10), .preset(and_1_out), .reset(clear));  // open: Qn
  and and_2 (and_2_out, ld, in_2);
  D_Flip_Flop d_ff_2 (.clk(clock), .D(out_10), .Q(out_11), .preset(and_2_out), .reset(clear));  // open: Qn
  and and_3 (and_3_out, ld, in_3);
  D_Flip_Flop d_ff_3 (.clk(clock), .D(out_11), .Q(out_12), .preset(and_3_out), .reset(clear));  // open: Qn
  and and_4 (and_4_out, ld, in_4);
  D_Flip_Flop d_ff_4 (.clk(clock), .D(out_12), .Q(out_13), .preset(and_4_out), .reset(clear));  // open: Qn
  and and_5 (and_5_out, ld, in_5);
  D_Flip_Flop d_ff_5 (.clk(clock), .D(out_13), .Q(out_14), .preset(and_5_out), .reset(clear));  // open: Qn
  and and_6 (and_6_out, ld, in_6);
  D_Flip_Flop d_ff_6 (.clk(clock), .D(out_14), .Q(out_15), .preset(and_6_out), .reset(clear));  // open: Qn
endmodule
