// Logisim project q01.circ as structural Verilog: 1 circuit, main circuit main
module main (
  input  a,
  output A_2,
  output B
);

  wire clock_1_out, d_ff_1_qn;

  Clock clock_1 (.out(clock_1_out));
  D_Flip_Flop d_ff_1 (.clk(clock_1_out), .D(a), .Q(A_2), .Qn(d_ff_1_qn));  // open: preset, reset
  D_Flip_Flop d_ff_2 (.clk(clock_1_out), .D(d_ff_1_qn), .Q(B));  // open: Qn, preset, reset
endmodule
