// Logisim project CIRCUITOS.circ as structural Verilog
module Q04A (
  input  A,
  input  B,
  input  C,
  output out_4
);

  wire nor_1_out, nor_2_out, nor_3_out, nor_4_out, nor_5_out;

  nor nor_1 (nor_1_out, A, A);
  nor nor_2 (nor_2_out, B, nor_3_out);
  nor nor_3 (nor_3_out, A, A);
  nor nor_4 (nor_4_out, B, nor_1_out);
  nor nor_5 (nor_5_out, C, nor_4_out);
  nor nor_6 (out_4, nor_5_out, nor_2_out);
endmodule

module Q04B (
  input  A,
  input  B,
  input  C,
  output out_4
);

  wire nand_1_out, nand_2_out, nand_3_out, nand_5_out;

  nand nand_1 (nand_1_out, A, A);
  nand nand_2 (nand_2_out, B, B);
  nand nand_3 (nand_3_out, B, nand_1_out);
  nand nand_4 (out_4, nand_3_out, nand_5_out);
  nand nand_5 (nand_5_out, A, nand_2_out);
endmodule

module Q04C (
  input  a,
  input  b,
  input  c,
  output x
);

  wire and_1_out, and_2_out, and_3_out, not_1_out, not_2_out, not_3_out;

  not not_1 (not_1_out, a);
  not not_2 (not_2_out, c);
  not not_3 (not_3_out, a);
  and and_1 (and_1_out, not_1_out, not_2_out);
  and and_2 (and_2_out, not_3_out, b);
  and and_3 (and_3_out, a, c);
  or or_1 (x, and_1_out, and_2_out, and_3_out);
endmodule
