// Logisim project ARQ II.circ as structural Verilog
module meio_somador (
  input  A0,
  input  B0,
  output S0,
  output CARRY_OUT
);

  and and_1 (CARRY_OUT, B0, A0);
  xor xor_1 (S0, A0, B0);
endmodule

module somador_completo (
  input  CARRY_IN,
  input  A0,
  input  B0,
  output S0,
  output CARRY_OUT
);

  wire meio_somador_1_carry_out, meio_somador_1_s0, meio_somador_2_carry_out;

  meio_somador meio_somador_1 (.A0(A0), .B0(B0), .CARRY_OUT(meio_somador_1_carry_out), .S0(meio_somador_1_s0));
  or or_1 (CARRY_OUT, meio_somador_1_carry_out, meio_somador_2_carry_out);
  meio_somador meio_somador_2 (.A0(CARRY_IN), .B0(meio_somador_1_s0), .CARRY_OUT(meio_somador_2_carry_out), .S0(S0));
endmodule

module soma_4bits (
  input  CARRY_IN,
  input  A0,
  input  A1,
  input  A2,
  input  A3,
  input  B0,
  input  B1,
  input  B2,
  input  B3,
  output S0,
  output S1,
  output S2,
  output S3,
  output CARRY_OUT
);

  wire somador_completo_1_carry_out, somador_completo_2_carry_out, somador_completo_3_carry_out;

  somador_completo somador_completo_1 (
    .CARRY_IN(CARRY_IN), .A0(A0), .B0(B0), .CARRY_OUT(somador_completo_1_carry_out), .S0(S0));
  somador_completo somador_completo_2 (
    .CARRY_IN(somador_completo_1_carry_out), .A0(A1), .B0(B1), .CARRY_OUT(somador_completo_2_carry_out),
    .S0(S1));
  somador_completo somador_completo_3 (
    .CARRY_IN(somador_completo_2_carry_out), .A0(A2), .B0(B2), .CARRY_OUT(somador_completo_3_carry_out),
    .S0(S2));
  somador_completo somador_completo_4 (
    .CARRY_IN(somador_completo_3_carry_out), .A0(A3), .B0(B3), .CARRY_OUT(CARRY_OUT), .S0(S3));
endmodule

module calculadora (
  input  A0,
  input  CARRY_IN,
  input  A1,
  input  A2,
  input  A3,
  input  B0,
  input  B1,
  input  B2,
  input  B3,
  output S0,
  output S1,
  output S2,
  output S3,
  output CARRY_OUT
);

  wire decoder_1_out0, decoder_1_out1, decoder_1_out2, decoder_1_out3, decoder_1_out4, decoder_1_out5,
       decoder_1_out6, decoder_1_out7;

  Decoder #(.select(3), .enable("false")) decoder_1 (
    .out0(decoder_1_out0), .out1(decoder_1_out1), .out2(decoder_1_out2), .out3(decoder_1_out3),
    .out4(decoder_1_out4), .out5(decoder_1_out5), .out6(decoder_1_out6), .out7(decoder_1_out7));  // open: sel
  soma_4bits soma_4bits_1 (
    .S0(S0), .S1(S1), .S2(S2), .S3(S3), .CARRY_OUT(CARRY_OUT), .CARRY_IN(CARRY_IN), .A0(A0), .A1(A1),
    .A2(A2), .A3(A3), .B0(B0), .B1(B1), .B2(B2), .B3(B3));
  _7_Segment_Display u_7_segment_display_1 (
    .g(decoder_1_out3), .f(decoder_1_out2), .a(decoder_1_out1), .b(decoder_1_out0), .e(decoder_1_out4),
    .d(decoder_1_out5), .c(decoder_1_out6), .dp(decoder_1_out7));
endmodule
